// Logisim project 1-to-2.circ as structural Verilog: 3 circuits, main circuit main
module main (
  input  in_1,
  output out_2,
  output out_3
);

  not not_1 (out_3, in_1);

  assign out_2 = in_1;
endmodule

module _1_to_2 (
  input  in_1,
  output out_2,
  output out_3
);

  not not_1 (out_3, in_1);

  assign out_2 = in_1;
endmodule

module _2_to_4 (
  input  in_1,
  input  in_2,
  output out_3,
  output out_4,
  output out_5,
  output out_6
);

  wire not_1_out, not_2_out;

  not not_1 (not_1_out, in_1);
  not not_2 (not_2_out, in_2);
  and and_1 (out_3, not_1_out, not_2_out);
  and and_2 (out_4, in_1, not_2_out);
  and and_3 (out_5, not_1_out, in_2);
  and and_4 (out_6, in_1, in_2);
endmodule
