// Logisim project 7bit.circ as structural Verilog
module main (
  input  [3:0] A,
  input  [3:0] B,
  output [4:0] SUM
);

  wire full_adder_1_cout, full_adder_2_cout, full_adder_3_cout;

  Full_Adder full_adder_1 (.A(1'b0), .B(A[0]), .Cin(B[0]), .S(SUM[0]), .Cout(full_adder_1_cout));
  Full_Adder full_adder_2 (.A(full_adder_1_cout), .B(A[1]), .Cin(B[1]), .S(SUM[1]), .Cout(full_adder_2_cout));
  Full_Adder full_adder_3 (.A(full_adder_2_cout), .B(A[2]), .Cin(B[2]), .S(SUM[2]), .Cout(full_adder_3_cout));
  Full_Adder full_adder_4 (.A(full_adder_3_cout), .B(A[3]), .Cin(B[3]), .S(SUM[3]), .Cout(SUM[4]));
endmodule

module Full_Adder (
  input  A,
  input  B,
  input  Cin,
  output S,
  output Cout
);

  wire and_1_out, and_2_out, xor_1_out;

  xor xor_1 (xor_1_out, A, B);
  xor xor_2 (S, xor_1_out, Cin);
  and and_1 (and_1_out, Cin, xor_1_out);
  and and_2 (and_2_out, B, A);
  or or_1 (Cout, and_1_out, and_2_out);
endmodule

module _7_bit (
  output S,
  output C
);
endmodule

module segment_display (
  input  D,
  input  C,
  input  B,
  input  A
);

  wire and_1_out, and_2_out, and_3_out, and_4_out, and_5_out, and_6_out, and_7_out, and_8_out, and_9_out,
       and_10_out, and_11_out, and_12_out, and_13_out, and_14_out, and_15_out, and_16_out, and_17_out,
       not_1_out, not_2_out, not_3_out, not_4_out, not_5_out, not_6_out, not_7_out, not_8_out, not_9_out,
       not_10_out, not_11_out, not_12_out, not_13_out, not_14_out, not_15_out, not_16_out, not_17_out,
       not_18_out, not_19_out, not_20_out, not_21_out, or_1_out, or_2_out, or_3_out, or_4_out, or_5_out,
       or_6_out, or_7_out, or_8_out, or_9_out, or_10_out, or_11_out, or_12_out, or_13_out, or_14_out,
       or_15_out, or_16_out, or_17_out;

  not not_1 (not_1_out, C);
  and and_1 (and_1_out, not_1_out, not_2_out);
  not not_2 (not_2_out, A);
  and and_2 (and_2_out, C, A);
  not not_3 (not_3_out, C);
  not not_4 (not_4_out, B);
  and and_3 (and_3_out, not_4_out, not_5_out);
  not not_5 (not_5_out, A);
  not not_6 (not_6_out, B);
  or or_1 (or_1_out, not_6_out, A);
  not not_7 (not_7_out, C);
  and and_4 (and_4_out, not_7_out, not_8_out);
  not not_8 (not_8_out, A);
  not not_9 (not_9_out, C);
  and and_5 (and_5_out, not_9_out, B);
  not not_10 (not_10_out, A);
  and and_6 (and_6_out, C, not_11_out);
  not not_11 (not_11_out, B);
  not not_12 (not_12_out, C);
  and and_7 (and_7_out, not_12_out, not_13_out);
  not not_13 (not_13_out, A);
  and and_8 (and_8_out, B, not_14_out);
  not not_14 (not_14_out, A);
  not not_15 (not_15_out, B);
  and and_9 (and_9_out, not_15_out, not_16_out);
  not not_16 (not_16_out, A);
  and and_10 (and_10_out, C, not_17_out);
  not not_17 (not_17_out, B);
  and and_11 (and_11_out, C, not_18_out);
  not not_18 (not_18_out, A);
  not not_19 (not_19_out, C);
  and and_12 (and_12_out, not_19_out, B);
  and and_13 (and_13_out, B, not_20_out);
  not not_20 (not_20_out, A);
  and and_14 (and_14_out, C, not_21_out);
  not not_21 (not_21_out, B);
  or or_2 (or_2_out, and_1_out, B);
  or or_3 (or_3_out, and_2_out, D);
  or or_4 (or_4_out, not_3_out, and_3_out);
  and and_15 (and_15_out, B, A);
  or or_5 (or_5_out, or_1_out, C);
  or or_6 (or_6_out, and_4_out, and_5_out);
  and and_16 (and_16_out, B, not_10_out);
  and and_17 (and_17_out, and_6_out, A);
  or or_7 (or_7_out, and_7_out, and_8_out);
  or or_8 (or_8_out, and_9_out, and_10_out);
  or or_9 (or_9_out, and_11_out, D);
  or or_10 (or_10_out, and_12_out, and_13_out);
  or or_11 (or_11_out, and_14_out, D);
  or or_12 (or_12_out, or_2_out, or_3_out);
  or or_13 (or_13_out, or_4_out, and_15_out);
  or or_14 (or_14_out, or_6_out, and_16_out);
  or or_15 (or_15_out, and_17_out, D);
  or or_16 (or_16_out, or_8_out, or_9_out);
  or or_17 (or_17_out, or_10_out, or_11_out);
  or or_18 (or_7_out, or_14_out, or_15_out);
  _7_Segment_Display u_7_segment_display_1 (
    .g(or_17_out), .f(or_16_out), .a(or_12_out), .b(or_13_out), .e(or_7_out), .d(or_7_out), .c(or_5_out));  // open: dp
endmodule

module display_with_addition (
  input  [2:0] in_1
);

  wire decoder_1_a1, decoder_1_a2, decoder_1_a3, decoder_1_a4, decoder_1_b1, decoder_1_b2, decoder_1_b3;

  _7_Segment_Display u_7_segment_display_1 (
    .g(decoder_1_b3), .f(decoder_1_b2), .a(decoder_1_a1), .b(decoder_1_a2), .e(decoder_1_b1),
    .d(decoder_1_a4), .c(decoder_1_a3));  // open: dp
  decoder decoder_1 (
    .A(1'b0), .B(in_1[2]), .C(in_1[1]), .D(in_1[0]), .A1(decoder_1_a1), .A2(decoder_1_a2), .A3(decoder_1_a3),
    .A4(decoder_1_a4), .B1(decoder_1_b1), .B2(decoder_1_b2), .B3(decoder_1_b3));  // open: E, B4
endmodule

module decoder (
  input  A,
  input  B,
  input  C,
  input  D,
  input  E,
  output A1,
  output A2,
  output A3,
  output A4,
  output B1,
  output B2,
  output B3,
  output B4
);

  wire and_1_out, and_2_out, and_3_out, and_4_out, and_5_out, and_6_out, and_7_out, and_8_out, and_9_out,
       and_10_out, and_11_out, and_12_out, and_13_out, and_14_out, and_15_out, and_16_out, and_17_out,
       and_18_out, and_19_out, and_20_out, and_21_out, and_22_out, and_23_out, and_24_out, and_25_out,
       and_26_out, and_27_out, and_28_out, and_29_out, and_30_out, and_31_out, and_32_out, and_33_out,
       and_34_out, and_35_out, not_1_out, not_2_out, not_3_out, not_4_out, not_5_out, not_6_out, not_7_out,
       not_8_out, not_9_out, not_10_out, not_11_out, not_12_out, not_13_out, not_14_out, not_15_out,
       not_16_out, not_17_out, not_18_out, not_19_out, not_20_out, not_21_out, not_22_out, not_23_out,
       not_24_out, not_25_out, or_1_out, or_2_out, or_3_out, or_4_out, or_6_out, or_10_out, or_11_out;

  not not_1 (not_1_out, A);
  not not_2 (not_2_out, C);
  not not_3 (not_3_out, D);
  not not_4 (not_4_out, B);
  not not_5 (not_5_out, C);
  not not_6 (not_6_out, A);
  not not_7 (not_7_out, B);
  not not_8 (not_8_out, A);
  not not_9 (not_9_out, C);
  not not_10 (not_10_out, A);
  not not_11 (not_11_out, B);
  not not_12 (not_12_out, B);
  not not_13 (not_13_out, B);
  not not_14 (not_14_out, B);
  not not_15 (not_15_out, C);
  and and_1 (and_1_out, not_1_out, B);
  and and_2 (and_2_out, not_2_out, not_3_out);
  and and_3 (and_3_out, A, not_4_out);
  and and_4 (and_4_out, not_5_out, D);
  not not_16 (not_16_out, D);
  and and_5 (and_5_out, not_6_out, not_7_out);
  and and_6 (and_6_out, not_8_out, C);
  and and_7 (and_7_out, A, not_9_out);
  not not_17 (not_17_out, D);
  and and_8 (and_8_out, A, B);
  not not_18 (not_18_out, C);
  and and_9 (and_9_out, not_10_out, not_11_out);
  and and_10 (and_10_out, not_12_out, C);
  not not_19 (not_19_out, A);
  not not_20 (not_20_out, D);
  not not_21 (not_21_out, B);
  not not_22 (not_22_out, C);
  not not_23 (not_23_out, D);
  not not_24 (not_24_out, C);
  and and_11 (and_11_out, not_13_out, C);
  and and_12 (and_12_out, A, B);
  not not_25 (not_25_out, A);
  and and_13 (and_13_out, not_14_out, not_15_out);
  and and_14 (and_14_out, B, C);
  and and_15 (and_15_out, and_1_out, and_2_out);
  or or_1 (or_1_out, and_15_out, and_16_out);
  and and_16 (and_16_out, and_3_out, and_4_out);
  and and_17 (and_17_out, A, B);
  and and_18 (and_18_out, and_17_out, and_19_out);
  and and_19 (and_19_out, C, not_16_out);
  and and_20 (and_20_out, and_5_out, C);
  or or_2 (or_2_out, and_20_out, and_21_out);
  and and_21 (and_21_out, and_6_out, D);
  and and_22 (and_22_out, and_7_out, not_17_out);
  or or_3 (or_3_out, and_22_out, and_23_out);
  and and_23 (and_23_out, and_8_out, not_18_out);
  and and_24 (and_24_out, and_9_out, D);
  or or_4 (or_4_out, and_24_out, and_25_out);
  and and_25 (and_25_out, and_10_out, D);
  and and_26 (and_26_out, not_19_out, B);
  and and_27 (and_27_out, and_26_out, and_28_out);
  and and_28 (and_28_out, C, not_20_out);
  and and_29 (and_29_out, A, not_21_out);
  and and_30 (and_30_out, and_29_out, and_31_out);
  and and_31 (and_31_out, not_22_out, not_23_out);
  and and_32 (and_32_out, A, B);
  and and_33 (and_33_out, and_32_out, and_34_out);
  and and_34 (and_34_out, not_24_out, D);
  or or_5 (B3, and_11_out, and_12_out);
  or or_6 (or_6_out, not_25_out, and_13_out);
  or or_7 (B4, or_6_out, and_35_out);
  and and_35 (and_35_out, and_14_out, D);
  or or_8 (A1, or_1_out, and_18_out);
  or or_9 (A2, or_2_out, or_3_out);
  or or_10 (or_10_out, or_4_out, and_27_out);
  or or_11 (or_11_out, and_30_out, and_33_out);
  or or_12 (A3, or_10_out, or_11_out);

  assign A4 = E;
  assign B1 = 1'b0;
  assign B2 = 1'b0;
endmodule

module _9_number (
  input  D,
  input  C,
  input  B,
  input  A,
  output a_2,
  output b_2,
  output c_2,
  output d_2,
  output e,
  output f,
  output g
);

  wire and_1_out, and_2_out, and_3_out, and_4_out, and_5_out, and_6_out, and_7_out, and_8_out, and_9_out,
       and_10_out, and_11_out, and_12_out, and_13_out, and_14_out, and_15_out, and_16_out, and_17_out,
       and_18_out, not_1_out, not_2_out, not_3_out, not_4_out, not_5_out, not_6_out, not_7_out, not_8_out,
       not_9_out, not_10_out, not_11_out, not_12_out, not_13_out, not_14_out, not_15_out, not_16_out,
       not_17_out, not_18_out, not_19_out, not_20_out, not_21_out, or_1_out, or_2_out, or_3_out, or_4_out,
       or_5_out, or_6_out, or_8_out, or_9_out, or_10_out, or_11_out, or_12_out, or_13_out, or_16_out,
       or_17_out;

  not not_1 (not_1_out, C);
  and and_1 (and_1_out, not_1_out, not_2_out);
  not not_2 (not_2_out, A);
  and and_2 (and_2_out, C, A);
  not not_3 (not_3_out, C);
  not not_4 (not_4_out, B);
  and and_3 (and_3_out, not_4_out, not_5_out);
  not not_5 (not_5_out, A);
  and and_4 (and_4_out, B, A);
  not not_6 (not_6_out, B);
  or or_1 (or_1_out, not_6_out, A);
  or or_2 (or_2_out, C, D);
  not not_7 (not_7_out, C);
  and and_5 (and_5_out, not_7_out, not_8_out);
  not not_8 (not_8_out, A);
  not not_9 (not_9_out, C);
  and and_6 (and_6_out, not_9_out, B);
  not not_10 (not_10_out, A);
  and and_7 (and_7_out, C, not_11_out);
  not not_11 (not_11_out, B);
  not not_12 (not_12_out, C);
  and and_8 (and_8_out, not_12_out, not_13_out);
  not not_13 (not_13_out, A);
  and and_9 (and_9_out, B, not_14_out);
  not not_14 (not_14_out, A);
  not not_15 (not_15_out, B);
  and and_10 (and_10_out, not_15_out, not_16_out);
  not not_16 (not_16_out, A);
  and and_11 (and_11_out, C, not_17_out);
  not not_17 (not_17_out, B);
  and and_12 (and_12_out, C, not_18_out);
  not not_18 (not_18_out, A);
  not not_19 (not_19_out, C);
  and and_13 (and_13_out, not_19_out, B);
  and and_14 (and_14_out, B, not_20_out);
  not not_20 (not_20_out, A);
  and and_15 (and_15_out, C, not_21_out);
  not not_21 (not_21_out, B);
  or or_3 (or_3_out, and_1_out, B);
  or or_4 (or_4_out, and_2_out, D);
  or or_5 (or_5_out, not_3_out, and_3_out);
  or or_6 (or_6_out, and_4_out, D);
  or or_7 (c_2, or_1_out, or_2_out);
  or or_8 (or_8_out, and_5_out, and_6_out);
  and and_16 (and_16_out, B, not_10_out);
  and and_17 (and_17_out, and_7_out, A);
  or or_9 (or_9_out, and_8_out, and_9_out);
  and and_18 (and_18_out, D, B);
  or or_10 (or_10_out, and_10_out, and_11_out);
  or or_11 (or_11_out, and_12_out, D);
  or or_12 (or_12_out, and_13_out, and_14_out);
  or or_13 (or_13_out, and_15_out, D);
  or or_14 (a_2, or_3_out, or_4_out);
  or or_15 (b_2, or_5_out, or_6_out);
  or or_16 (or_16_out, or_8_out, and_16_out);
  or or_17 (or_17_out, and_17_out, D);
  or or_18 (e, or_9_out, and_18_out);
  or or_19 (f, or_10_out, or_11_out);
  or or_20 (g, or_12_out, or_13_out);
  or or_21 (d_2, or_16_out, or_17_out);
endmodule

module \final  (
  input  [3:0] in_1,
  input  [3:0] in_2
);

  wire divider_1_a1, divider_1_a2, divider_1_a3, divider_1_a4, divider_1_b1, divider_1_b2, divider_1_b3,
       divider_1_b4, divider_2_a1, divider_2_a2, divider_2_a3, divider_2_a4, divider_2_b1, divider_2_b2,
       divider_2_b3, divider_2_b4, divider_3_a1, divider_3_a2, divider_3_a3, divider_3_a4, divider_3_b1,
       divider_3_b2, divider_3_b3, divider_3_b4, n9_number_1_a_2, n9_number_1_b_2, n9_number_1_c_2,
       n9_number_1_d_2, n9_number_1_f, n9_number_1_g, n9_number_2_a_2, n9_number_2_b_2, n9_number_2_c_2,
       n9_number_2_d_2, n9_number_2_e, n9_number_2_f, n9_number_2_g, n9_number_3_a_2, n9_number_3_b_2,
       n9_number_3_c_2, n9_number_3_d_2, n9_number_3_e, n9_number_3_f, n9_number_3_g, n9_number_4_a_2,
       n9_number_4_b_2, n9_number_4_c_2, n9_number_4_d_2, n9_number_4_e, n9_number_4_f, n9_number_4_g,
       n9_number_5_a_2, n9_number_5_b_2, n9_number_5_c_2, n9_number_5_d_2, n9_number_5_e, n9_number_5_f,
       n9_number_5_g, n9_number_6_a_2, n9_number_6_b_2, n9_number_6_c_2, n9_number_6_d_2, n9_number_6_e,
       n9_number_6_f, n9_number_6_g;
  wire [4:0] main_1_sum;

  _9_number u_9_number_1 (
    .D(divider_1_b1), .C(divider_1_b2), .B(divider_1_b3), .A(divider_1_b4), .a_2(n9_number_1_a_2),
    .b_2(n9_number_1_b_2), .c_2(n9_number_1_c_2), .d_2(n9_number_1_d_2), .e(n9_number_1_d_2),
    .f(n9_number_1_f), .g(n9_number_1_g));
  _7_Segment_Display u_7_segment_display_1 (
    .g(n9_number_2_g), .f(n9_number_2_f), .a(n9_number_2_a_2), .b(n9_number_2_b_2), .e(n9_number_2_e),
    .d(n9_number_2_d_2), .c(n9_number_2_c_2));  // open: dp
  _7_Segment_Display u_7_segment_display_2 (
    .g(n9_number_1_g), .f(n9_number_1_f), .a(n9_number_1_a_2), .b(n9_number_1_b_2), .e(n9_number_1_d_2),
    .d(n9_number_1_d_2), .c(n9_number_1_c_2));  // open: dp
  DIVIDER divider_1 (
    .A(1'b0), .B(in_1[3]), .C(in_1[2]), .D(in_1[1]), .E(in_1[0]), .A1(divider_1_a1), .A2(divider_1_a2),
    .A3(divider_1_a3), .A4(divider_1_a4), .B1(divider_1_b1), .B2(divider_1_b2), .B3(divider_1_b3),
    .B4(divider_1_b4));
  _9_number u_9_number_2 (
    .D(divider_1_a1), .C(divider_1_a2), .B(divider_1_a3), .A(divider_1_a4), .a_2(n9_number_2_a_2),
    .b_2(n9_number_2_b_2), .c_2(n9_number_2_c_2), .d_2(n9_number_2_d_2), .e(n9_number_2_e),
    .f(n9_number_2_f), .g(n9_number_2_g));
  _9_number u_9_number_3 (
    .D(divider_2_b1), .C(divider_2_b2), .B(divider_2_b3), .A(divider_2_b4), .a_2(n9_number_3_a_2),
    .b_2(n9_number_3_b_2), .c_2(n9_number_3_c_2), .d_2(n9_number_3_d_2), .e(n9_number_3_e),
    .f(n9_number_3_f), .g(n9_number_3_g));
  _7_Segment_Display u_7_segment_display_3 (
    .g(n9_number_4_g), .f(n9_number_4_f), .a(n9_number_4_a_2), .b(n9_number_4_b_2), .e(n9_number_4_e),
    .d(n9_number_4_d_2), .c(n9_number_4_c_2));  // open: dp
  _7_Segment_Display u_7_segment_display_4 (
    .g(n9_number_3_g), .f(n9_number_3_f), .a(n9_number_3_a_2), .b(n9_number_3_b_2), .e(n9_number_3_e),
    .d(n9_number_3_d_2), .c(n9_number_3_c_2));  // open: dp
  DIVIDER divider_2 (
    .A(1'b0), .B(in_2[3]), .C(in_2[2]), .D(in_2[1]), .E(in_2[0]), .A1(divider_2_a1), .A2(divider_2_a2),
    .A3(divider_2_a3), .A4(divider_2_a4), .B1(divider_2_b1), .B2(divider_2_b2), .B3(divider_2_b3),
    .B4(divider_2_b4));
  _9_number u_9_number_4 (
    .D(divider_2_a1), .C(divider_2_a2), .B(divider_2_a3), .A(divider_2_a4), .a_2(n9_number_4_a_2),
    .b_2(n9_number_4_b_2), .c_2(n9_number_4_c_2), .d_2(n9_number_4_d_2), .e(n9_number_4_e),
    .f(n9_number_4_f), .g(n9_number_4_g));
  main main_1 (.A(in_1), .B(in_2), .SUM(main_1_sum));
  _9_number u_9_number_5 (
    .D(divider_3_b1), .C(divider_3_b2), .B(divider_3_b3), .A(divider_3_b4), .a_2(n9_number_5_a_2),
    .b_2(n9_number_5_b_2), .c_2(n9_number_5_c_2), .d_2(n9_number_5_d_2), .e(n9_number_5_e),
    .f(n9_number_5_f), .g(n9_number_5_g));
  _7_Segment_Display u_7_segment_display_5 (
    .g(n9_number_5_g), .f(n9_number_5_f), .a(n9_number_5_a_2), .b(n9_number_5_b_2), .e(n9_number_5_e),
    .d(n9_number_5_d_2), .c(n9_number_5_c_2));  // open: dp
  DIVIDER divider_3 (
    .A(main_1_sum[4]), .B(main_1_sum[3]), .C(main_1_sum[2]), .D(main_1_sum[1]), .E(main_1_sum[0]),
    .A1(divider_3_a1), .A2(divider_3_a2), .A3(divider_3_a3), .A4(divider_3_a4), .B1(divider_3_b1),
    .B2(divider_3_b2), .B3(divider_3_b3), .B4(divider_3_b4));
  _9_number u_9_number_6 (
    .D(divider_3_a1), .C(divider_3_a2), .B(divider_3_a3), .A(divider_3_a4), .a_2(n9_number_6_a_2),
    .b_2(n9_number_6_b_2), .c_2(n9_number_6_c_2), .d_2(n9_number_6_d_2), .e(n9_number_6_e),
    .f(n9_number_6_f), .g(n9_number_6_g));
  _7_Segment_Display u_7_segment_display_6 (
    .g(n9_number_6_g), .f(n9_number_6_f), .a(n9_number_6_a_2), .b(n9_number_6_b_2), .e(n9_number_6_e),
    .d(n9_number_6_d_2), .c(n9_number_6_c_2));  // open: dp
endmodule

module DIVIDER (
  input  A,
  input  B,
  input  C,
  input  D,
  input  E,
  output A1,
  output A2,
  output A3,
  output A4,
  output B1,
  output B2,
  output B3,
  output B4
);

  wire and_1_out, and_2_out, and_3_out, and_4_out, and_5_out, and_6_out, and_7_out, and_8_out, and_9_out,
       and_10_out, and_11_out, and_12_out, and_13_out, and_14_out, and_15_out, and_16_out, and_17_out,
       and_18_out, and_19_out, and_20_out, and_21_out, and_22_out, and_23_out, and_24_out, and_25_out,
       and_26_out, and_27_out, and_28_out, and_29_out, and_30_out, and_31_out, and_32_out, and_33_out,
       and_34_out, and_35_out, and_36_out, and_37_out, and_38_out, and_39_out, and_40_out, not_1_out,
       not_2_out, not_3_out, not_4_out, not_5_out, not_6_out, not_7_out, not_8_out, not_9_out, not_10_out,
       not_11_out, not_12_out, not_13_out, not_14_out, not_15_out, not_16_out, not_17_out, not_18_out,
       not_19_out, not_20_out, not_21_out, not_22_out, not_23_out, not_24_out, not_25_out, or_2_out,
       or_3_out, or_4_out, or_5_out, or_6_out, or_7_out, or_10_out, or_11_out;

  not not_1 (not_1_out, A);
  not not_2 (not_2_out, C);
  not not_3 (not_3_out, D);
  not not_4 (not_4_out, B);
  not not_5 (not_5_out, C);
  not not_6 (not_6_out, A);
  not not_7 (not_7_out, B);
  not not_8 (not_8_out, A);
  not not_9 (not_9_out, C);
  not not_10 (not_10_out, A);
  not not_11 (not_11_out, B);
  not not_12 (not_12_out, B);
  and and_1 (and_1_out, A, C);
  and and_2 (and_2_out, A, B);
  not not_13 (not_13_out, A);
  not not_14 (not_14_out, A);
  not not_15 (not_15_out, B);
  and and_3 (and_3_out, not_1_out, B);
  and and_4 (and_4_out, not_2_out, not_3_out);
  and and_5 (and_5_out, A, not_4_out);
  and and_6 (and_6_out, not_5_out, D);
  not not_16 (not_16_out, D);
  and and_7 (and_7_out, not_6_out, not_7_out);
  and and_8 (and_8_out, not_8_out, C);
  and and_9 (and_9_out, A, not_9_out);
  not not_17 (not_17_out, D);
  and and_10 (and_10_out, A, B);
  not not_18 (not_18_out, C);
  and and_11 (and_11_out, not_10_out, not_11_out);
  and and_12 (and_12_out, not_12_out, C);
  not not_19 (not_19_out, A);
  not not_20 (not_20_out, D);
  not not_21 (not_21_out, B);
  not not_22 (not_22_out, C);
  not not_23 (not_23_out, D);
  not not_24 (not_24_out, C);
  or or_1 (B3, and_1_out, and_2_out);
  and and_13 (and_13_out, not_13_out, B);
  and and_14 (and_14_out, not_14_out, B);
  and and_15 (and_15_out, B, C);
  and and_16 (and_16_out, A, not_15_out);
  not not_25 (not_25_out, C);
  and and_17 (and_17_out, and_3_out, and_4_out);
  or or_2 (or_2_out, and_17_out, and_18_out);
  and and_18 (and_18_out, and_5_out, and_6_out);
  and and_19 (and_19_out, A, B);
  and and_20 (and_20_out, and_19_out, and_21_out);
  and and_21 (and_21_out, C, not_16_out);
  and and_22 (and_22_out, and_7_out, C);
  or or_3 (or_3_out, and_22_out, and_23_out);
  and and_23 (and_23_out, and_8_out, D);
  and and_24 (and_24_out, and_9_out, not_17_out);
  or or_4 (or_4_out, and_24_out, and_25_out);
  and and_25 (and_25_out, and_10_out, not_18_out);
  and and_26 (and_26_out, and_11_out, D);
  or or_5 (or_5_out, and_26_out, and_27_out);
  and and_27 (and_27_out, and_12_out, D);
  and and_28 (and_28_out, not_19_out, B);
  and and_29 (and_29_out, and_28_out, and_30_out);
  and and_30 (and_30_out, C, not_20_out);
  and and_31 (and_31_out, A, not_21_out);
  and and_32 (and_32_out, and_31_out, and_33_out);
  and and_33 (and_33_out, not_22_out, not_23_out);
  and and_34 (and_34_out, A, B);
  and and_35 (and_35_out, and_34_out, and_36_out);
  and and_36 (and_36_out, not_24_out, D);
  and and_37 (and_37_out, and_13_out, D);
  or or_6 (or_6_out, and_37_out, and_38_out);
  and and_38 (and_38_out, and_14_out, C);
  and and_39 (and_39_out, and_15_out, D);
  or or_7 (or_7_out, and_39_out, and_40_out);
  and and_40 (and_40_out, and_16_out, not_25_out);
  or or_8 (A1, or_2_out, and_20_out);
  or or_9 (A2, or_3_out, or_4_out);
  or or_10 (or_10_out, or_5_out, and_29_out);
  or or_11 (or_11_out, and_32_out, and_35_out);
  or or_12 (B4, or_6_out, or_7_out);
  or or_13 (A3, or_10_out, or_11_out);

  assign A4 = E;
  assign B1 = 1'b0;
  assign B2 = 1'b0;
endmodule
