// Logisim project Half Adder.circ as structural Verilog
module main (
  input  A,
  input  B,
  output S,
  output C
);

  Half_Adder_XOR HALF_ADDER (.A(A), .B(B), .S(S), .C(C));
endmodule

module Half_Adder (
  input  A,
  input  B,
  output S,
  output C
);

  wire and_1_out, and_2_out, not_1_out, not_2_out;

  not not_1 (not_1_out, A);
  not not_2 (not_2_out, B);
  and and_1 (and_1_out, not_1_out, B);
  and and_2 (and_2_out, A, not_2_out);
  and and_3 (C, A, B);
  or or_1 (S, and_1_out, and_2_out);
endmodule

module Half_Adder_XOR (
  input  A,
  input  B,
  output S,
  output C
);

  xor xor_1 (S, A, B);
  and and_1 (C, B, A);
endmodule

module main_2 (
  input  Inc,
  input  A0,
  input  A1,
  input  A2,
  input  A3,
  output S0,
  output S1,
  output S2,
  output S3,
  output Cout
);

  wire half_adder_1_c, half_adder_2_c, half_adder_3_c;

  Half_Adder half_adder_1 (.A(Inc), .B(A0), .S(S0), .C(half_adder_1_c));
  Half_Adder half_adder_2 (.A(half_adder_1_c), .B(A1), .S(S1), .C(half_adder_2_c));
  Half_Adder half_adder_3 (.A(half_adder_2_c), .B(A2), .S(S2), .C(half_adder_3_c));
  Half_Adder half_adder_4 (.A(half_adder_3_c), .B(A3), .S(S3), .C(Cout));
endmodule

module f (
  input  in_1,
  input  in_2,
  input  in_3,
  output f_out
);

  wire and_1_out, and_2_out, and_3_out, and_4_out, not_1_out, not_2_out, not_3_out;

  not not_1 (not_1_out, in_1);
  not not_2 (not_2_out, in_2);
  not not_3 (not_3_out, in_3);
  and and_1 (and_1_out, not_1_out, not_2_out, not_3_out);
  and and_2 (and_2_out, in_1, not_2_out, not_3_out);
  and and_3 (and_3_out, in_1, not_2_out, in_3);
  and and_4 (and_4_out, in_1, in_2, not_3_out);
  or or_1 (f_out, and_1_out, and_2_out, and_3_out, and_4_out);
endmodule

module a (
  input  in_1,
  input  in_2,
  input  in_3,
  output f_out
);

  wire and_1_out, and_2_out, and_3_out, and_4_out;

  // NOT_Gate not_1 has open pins: in=in_1, out=open
  // NOT_Gate not_2 has open pins: in=in_2, out=open
  // NOT_Gate not_3 has open pins: in=in_3, out=open
  // AND_Gate and_1 has open pins: out=and_1_out
  // AND_Gate and_2 has open pins: out=and_2_out
  // AND_Gate and_3 has open pins: out=and_3_out
  // AND_Gate and_4 has open pins: out=and_4_out
  or or_1 (f_out, and_1_out, and_2_out, and_3_out, and_4_out);
endmodule

module Multiplexer (
  input  in_1,
  input  in_2,
  input  in_3,
  input  in_4,
  input  in_5,
  input  in_6,
  input  in_7,
  input  in_8,
  input  [2:0] in_9
);

  wire multiplexer_1_out;

  Multiplexer_part #(.select(3)) multiplexer_1 (
    .in0(in_1), .in1(in_2), .in2(in_3), .in3(in_4), .in4(in_5), .in5(in_6), .in6(in_7), .in7(in_8),
    .out(multiplexer_1_out), .sel(in_9));  // open: en
  LED led_1 (.in(multiplexer_1_out));
endmodule
