// Logisim project NAND.circ as structural Verilog: 1 circuit, main circuit main
module main (
  input  in_1,
  input  in_2,
  output out_3,
  output out_4,
  output out_5
);

  wire nand_2_out, nand_3_out, nand_4_out;

  nand nand_1 (out_3, in_1, in_1);
  nand nand_2 (nand_2_out, in_1, in_2);
  nand nand_3 (nand_3_out, in_1, in_1);
  nand nand_4 (nand_4_out, in_2, in_2);
  nand nand_5 (out_4, nand_2_out, nand_2_out);
  nand nand_6 (out_5, nand_3_out, nand_4_out);
endmodule
